// Digital circuit 4bitRegister.dig as structural Verilog
module _4bitRegister (
  input  WE,
  input  OE,
  input  [3:0] Din,
  input  clock,
  output [3:0] Dout,
  output [3:0] data
);

  Register #(.Bits(4)) register_1 (.D(Din), .C(clock), .en(WE), .Q(data));
  assign Dout = OE ? data : 4'bz;  // Driver driver_1
endmodule
