// Digital circuit 8bitRegister.dig as structural Verilog
module _8bitRegister (
  input  WE,
  input  OE,
  input  [7:0] Din,
  input  clock,
  output [7:0] Dout,
  output [7:0] data
);

  Register #(.Bits(8)) register_1 (.D(Din), .C(clock), .en(WE), .Q(data));
  assign Dout = OE ? data : 8'bz;  // Driver driver_1
endmodule
