// Digital circuit ALU.dig as structural Verilog
module ALU (
  input  OE,
  input  [7:0] RegA,
  input  [7:0] RegB,
  output Carry,
  output [7:0] Dout,
  output [7:0] data
);

  Add #(.Bits(8)) add_1 (.a(RegA), .b(RegB), .c_i(1'b0), .s(data), .c_o(Carry));
  assign Dout = OE ? data : 8'bz;  // Driver driver_1

  // Notes on the sheet:
  //   OE: output enable
  //   data: 实验调试使用
endmodule
