// Digital circuit RAM.dig as structural Verilog
module RAM (
  input  [3:0] Addr,
  input  [7:0] Din,
  input  WE,
  input  OE,
  input  clock,
  output [7:0] Dout
);

  EEPROMDualPort #(.AddrBits(4), .Bits(8)) eepromdualport_1 (
    .A(Addr), .Din(Din), .str(WE), .C(clock), .ld(OE), .D(Dout));

  // Notes on the sheet:
  //   contents of eepromdualport_1 (hex, n*v repeats v):
  //   5*0,23
endmodule
