// Digital circuit latch锁存器.dig as structural Verilog
module \latch锁存器  (
  input  Din,
  input  WE,
  output Dout
);

  wire \与门_1_c , \与门_2_c , \或门_1_c , \非门_1_b , \非门_2_b ;

  \非门  \u_非门_1  (.A(Din), .B(\非门_1_b ));
  \与门  \u_与门_1  (.A(Din), .B(WE), .C(\与门_1_c ));
  \与门  \u_与门_2  (.A(\非门_1_b ), .B(WE), .C(\与门_2_c ));
  \或门  \u_或门_1  (.A(Dout), .B(\与门_1_c ), .C(\或门_1_c ));
  \非门  \u_非门_2  (.A(\与门_2_c ), .B(\非门_2_b ));
  \与门  \u_与门_3  (.A(\或门_1_c ), .B(\非门_2_b ), .C(Dout));

  // Notes on the sheet:
  //   Din: data input
  //   WE: write enable latch
endmodule
