// Digital circuit 上升沿锁存器.dig as structural Verilog
module \上升沿锁存器  (
  input  Din,
  input  clock,
  output Dout
);

  wire \latch锁存器_1_dout , \非门_1_b ;

  \非门  \u_非门_1  (.A(clock), .B(\非门_1_b ));
  \latch锁存器  \latch锁存器_1  (.Din(Din), .WE(\非门_1_b ), .Dout(\latch锁存器_1_dout ));
  \latch锁存器  \latch锁存器_2  (.Din(\latch锁存器_1_dout ), .WE(clock), .Dout(Dout));
endmodule
