// Digital circuit 使能寄存器.dig as structural Verilog
module \使能寄存器  (
  input  [7:0] Din,
  input  clock,
  input  En,
  output [7:0] Dout
);

  wire relaydt_1_p4;

  // RelayDT relaydt_1: pin names not known; wires that end beside it: En, clock, 1'b0, relaydt_1_p4
  PullDown pulldown_1 (.out(relaydt_1_p4));
  \上升沿锁存器  \u_上升沿锁存器_1  (.Din(Din[0]), .clock(relaydt_1_p4), .Dout(Dout[0]));
  \上升沿锁存器  \u_上升沿锁存器_2  (.Din(Din[1]), .clock(relaydt_1_p4), .Dout(Dout[1]));
  \上升沿锁存器  \u_上升沿锁存器_3  (.Din(Din[2]), .clock(relaydt_1_p4), .Dout(Dout[2]));
  \上升沿锁存器  \u_上升沿锁存器_4  (.Din(Din[3]), .clock(relaydt_1_p4), .Dout(Dout[3]));
  \上升沿锁存器  \u_上升沿锁存器_5  (.Din(Din[4]), .clock(relaydt_1_p4), .Dout(Dout[4]));
  \上升沿锁存器  \u_上升沿锁存器_6  (.Din(Din[5]), .clock(relaydt_1_p4), .Dout(Dout[5]));
  \上升沿锁存器  \u_上升沿锁存器_7  (.Din(Din[6]), .clock(relaydt_1_p4), .Dout(Dout[6]));
  \上升沿锁存器  \u_上升沿锁存器_8  (.Din(Din[7]), .clock(relaydt_1_p4), .Dout(Dout[7]));

  // Notes on the sheet:
  //   En: enable
endmodule
