// Digital circuit 全加器.dig as structural Verilog
module \全加器  (
  input  C,
  input  A,
  input  B,
  output SUM,
  output Carry
);

  wire \半加器_1_c , \半加器_1_sum , \半加器_2_c ;

  \半加器  \u_半加器_1  (.A(A), .B(B), .SUM(\半加器_1_sum ), .C(\半加器_1_c ));
  \半加器  \u_半加器_2  (.A(C), .B(\半加器_1_sum ), .SUM(SUM), .C(\半加器_2_c ));
  or or_1 (Carry, \半加器_2_c , \半加器_1_c );
endmodule
