// Digital circuit 内存单元.dig as structural Verilog
module \内存单元  (
  input  row,
  input  column,
  input  store,
  input  load,
  input  [7:0] Din,
  input  clock,
  output [7:0] Dout,
  output [7:0] data
);

  wire \与门_1_c , \与门_2_c , \与门_3_c ;

  \与门  \u_与门_1  (.A(row), .B(column), .C(\与门_1_c ));
  \与门  \u_与门_2  (.A(store), .B(\与门_1_c ), .C(\与门_2_c ));
  \与门  \u_与门_3  (.A(\与门_1_c ), .B(load), .C(\与门_3_c ));
  \输入输出使能寄存器  \u_输入输出使能寄存器_1  (.clock(clock), .Din(Din), .En(\与门_2_c ), .OE(\与门_3_c ), .Dout(Dout), .data(data));

  // Notes on the sheet:
  //   row: 行选
  //   column: 列选
endmodule
