// Digital circuit 内存条.dig as structural Verilog
module \内存条  (
  input  row0,
  input  row1,
  input  row2,
  input  row3,
  input  column0,
  input  column1,
  input  column2,
  input  column3,
  input  store,
  input  load,
  input  clock,
  input  [7:0] Din,
  output [7:0] out_13,
  output [7:0] out_14,
  output [7:0] out_15,
  output [7:0] out_16,
  output [7:0] out_17,
  output [7:0] out_18,
  output [7:0] out_19,
  output [7:0] out_20,
  output [7:0] out_21,
  output [7:0] out_22,
  output [7:0] out_23,
  output [7:0] out_24,
  output [7:0] out_25,
  output [7:0] out_26,
  output [7:0] out_27,
  output [7:0] out_28,
  output [7:0] Dout
);

  \内存单元  \u_内存单元_1  (
    .row(row0), .column(column0), .store(store), .load(load), .Din(Din), .clock(clock), .Dout(Dout),
    .data(out_13));
  \内存单元  \u_内存单元_2  (
    .row(row1), .column(column0), .store(store), .load(load), .Din(Din), .clock(clock), .Dout(Dout),
    .data(out_24));
  \内存单元  \u_内存单元_3  (
    .row(row2), .column(column0), .store(store), .load(load), .Din(Din), .clock(clock), .Dout(Dout),
    .data(out_23));
  \内存单元  \u_内存单元_4  (
    .row(row3), .column(column0), .store(store), .load(load), .Din(Din), .clock(clock), .Dout(Dout),
    .data(out_25));
  \内存单元  \u_内存单元_5  (
    .row(row0), .column(column1), .store(store), .load(load), .Din(Din), .clock(clock), .Dout(Dout),
    .data(out_14));
  \内存单元  \u_内存单元_6  (
    .row(row1), .column(column1), .store(store), .load(load), .Din(Din), .clock(clock), .Dout(Dout),
    .data(out_21));
  \内存单元  \u_内存单元_7  (
    .row(row2), .column(column1), .store(store), .load(load), .Din(Din), .clock(clock), .Dout(Dout),
    .data(out_22));
  \内存单元  \u_内存单元_8  (
    .row(row3), .column(column1), .store(store), .load(load), .Din(Din), .clock(clock), .Dout(Dout),
    .data(out_26));
  \内存单元  \u_内存单元_9  (
    .row(row0), .column(column2), .store(store), .load(load), .Din(Din), .clock(clock), .Dout(Dout),
    .data(out_15));
  \内存单元  \u_内存单元_10  (
    .row(row1), .column(column2), .store(store), .load(load), .Din(Din), .clock(clock), .Dout(Dout),
    .data(out_20));
  \内存单元  \u_内存单元_11  (
    .row(row2), .column(column2), .store(store), .load(load), .Din(Din), .clock(clock), .Dout(Dout),
    .data(out_19));
  \内存单元  \u_内存单元_12  (
    .row(row3), .column(column2), .store(store), .load(load), .Din(Din), .clock(clock), .Dout(Dout),
    .data(out_27));
  \内存单元  \u_内存单元_13  (
    .row(row0), .column(column3), .store(store), .load(load), .Din(Din), .clock(clock), .Dout(Dout),
    .data(out_16));
  \内存单元  \u_内存单元_14  (
    .row(row1), .column(column3), .store(store), .load(load), .Din(Din), .clock(clock), .Dout(Dout),
    .data(out_17));
  \内存单元  \u_内存单元_15  (
    .row(row2), .column(column3), .store(store), .load(load), .Din(Din), .clock(clock), .Dout(Dout),
    .data(out_18));
  \内存单元  \u_内存单元_16  (
    .row(row3), .column(column3), .store(store), .load(load), .Din(Din), .clock(clock), .Dout(Dout),
    .data(out_28));
endmodule
