// Digital circuit 寄存器.dig as structural Verilog
module \寄存器  (
  input  [7:0] Din,
  input  clock,
  output [7:0] Dout
);

  \上升沿锁存器  \u_上升沿锁存器_1  (.Din(Din[0]), .clock(clock), .Dout(Dout[0]));
  \上升沿锁存器  \u_上升沿锁存器_2  (.Din(Din[1]), .clock(clock), .Dout(Dout[1]));
  \上升沿锁存器  \u_上升沿锁存器_3  (.Din(Din[2]), .clock(clock), .Dout(Dout[2]));
  \上升沿锁存器  \u_上升沿锁存器_4  (.Din(Din[3]), .clock(clock), .Dout(Dout[3]));
  \上升沿锁存器  \u_上升沿锁存器_5  (.Din(Din[4]), .clock(clock), .Dout(Dout[4]));
  \上升沿锁存器  \u_上升沿锁存器_6  (.Din(Din[5]), .clock(clock), .Dout(Dout[5]));
  \上升沿锁存器  \u_上升沿锁存器_7  (.Din(Din[6]), .clock(clock), .Dout(Dout[6]));
  \上升沿锁存器  \u_上升沿锁存器_8  (.Din(Din[7]), .clock(clock), .Dout(Dout[7]));
endmodule
