// Digital circuit 寻址内存RAM.dig as structural Verilog
module \寻址内存RAM  (
  input  store,
  input  load,
  input  clock,
  input  [7:0] Din,
  input  [3:0] Addr,
  output [7:0] out_5,
  output [7:0] out_6,
  output [7:0] out_7,
  output [7:0] out_8,
  output [7:0] out_9,
  output [7:0] out_10,
  output [7:0] out_11,
  output [7:0] out_12,
  output [7:0] out_13,
  output [7:0] out_14,
  output [7:0] out_15,
  output [7:0] out_16,
  output [7:0] out_17,
  output [7:0] out_18,
  output [7:0] out_19,
  output [7:0] out_20,
  output [7:0] Dout
);

  wire column0, column1, column2, column3, row0, row1, row2, row3;

  Decoder #(.Selector_Bits(2)) decoder_1 (.sel(Addr[3:2]), .out_0(row0), .out_1(row1), .out_2(row2), .out_3(row3));
  Decoder #(.Selector_Bits(2)) decoder_2 (
    .sel(Addr[1:0]), .out_0(column0), .out_1(column1), .out_2(column2), .out_3(column3));
  \内存单元  \u_内存单元_1  (
    .row(row0), .column(column0), .store(store), .load(load), .Din(Din), .clock(clock), .Dout(Dout),
    .data(out_5));
  \内存单元  \u_内存单元_2  (
    .row(row1), .column(column0), .store(store), .load(load), .Din(Din), .clock(clock), .Dout(Dout),
    .data(out_16));
  \内存单元  \u_内存单元_3  (
    .row(row2), .column(column0), .store(store), .load(load), .Din(Din), .clock(clock), .Dout(Dout),
    .data(out_15));
  \内存单元  \u_内存单元_4  (
    .row(row3), .column(column0), .store(store), .load(load), .Din(Din), .clock(clock), .Dout(Dout),
    .data(out_17));
  \内存单元  \u_内存单元_5  (
    .row(row0), .column(column1), .store(store), .load(load), .Din(Din), .clock(clock), .Dout(Dout),
    .data(out_6));
  \内存单元  \u_内存单元_6  (
    .row(row1), .column(column1), .store(store), .load(load), .Din(Din), .clock(clock), .Dout(Dout),
    .data(out_13));
  \内存单元  \u_内存单元_7  (
    .row(row2), .column(column1), .store(store), .load(load), .Din(Din), .clock(clock), .Dout(Dout),
    .data(out_14));
  \内存单元  \u_内存单元_8  (
    .row(row3), .column(column1), .store(store), .load(load), .Din(Din), .clock(clock), .Dout(Dout),
    .data(out_18));
  \内存单元  \u_内存单元_9  (
    .row(row0), .column(column2), .store(store), .load(load), .Din(Din), .clock(clock), .Dout(Dout),
    .data(out_7));
  \内存单元  \u_内存单元_10  (
    .row(row1), .column(column2), .store(store), .load(load), .Din(Din), .clock(clock), .Dout(Dout),
    .data(out_12));
  \内存单元  \u_内存单元_11  (
    .row(row2), .column(column2), .store(store), .load(load), .Din(Din), .clock(clock), .Dout(Dout),
    .data(out_11));
  \内存单元  \u_内存单元_12  (
    .row(row3), .column(column2), .store(store), .load(load), .Din(Din), .clock(clock), .Dout(Dout),
    .data(out_19));
  \内存单元  \u_内存单元_13  (
    .row(row0), .column(column3), .store(store), .load(load), .Din(Din), .clock(clock), .Dout(Dout),
    .data(out_8));
  \内存单元  \u_内存单元_14  (
    .row(row1), .column(column3), .store(store), .load(load), .Din(Din), .clock(clock), .Dout(Dout),
    .data(out_9));
  \内存单元  \u_内存单元_15  (
    .row(row2), .column(column3), .store(store), .load(load), .Din(Din), .clock(clock), .Dout(Dout),
    .data(out_10));
  \内存单元  \u_内存单元_16  (
    .row(row3), .column(column3), .store(store), .load(load), .Din(Din), .clock(clock), .Dout(Dout),
    .data(out_20));

  // Notes on the sheet:
  //   行选
  //   列选
endmodule
