// Digital circuit 计算机体系结构.dig as structural Verilog
module \计算机体系结构  (
  input  RegA_WE,
  input  RegA_OE,
  input  RegB_WE,
  input  RegB_OE,
  input  ALU_OE,
  input  RegA_WE_2,
  input  RegA_OE_2,
  input  MBR_WE,
  input  MBR_OE,
  input  Memory_WE,
  input  Memory_OE,
  input  IR_OE,
  input  IR_WE,
  input  MAR_OE,
  input  MAR_WE,
  input  PC_OE,
  input  PC_EN,
  output [7:0] out_5,
  output [7:0] out_6,
  output [7:0] out_10,
  output [7:0] out_11,
  output [7:0] out_14,
  output [7:0] out_18,
  output [3:0] addr,
  output [3:0] PC
);

  wire clock;
  wire [3:0] MAR_dout;
  wire [7:0] alu_1_dout, IR_dout, OutputReg_dout, RegA_dout, RegB_dout;

  _8bitRegister RegA (.WE(RegA_WE), .OE(RegA_OE), .Din(OutputReg_dout), .clock(clock), .Dout(RegA_dout), .data(out_5));
  _8bitRegister RegB (.WE(RegB_WE), .OE(RegB_OE), .Din(OutputReg_dout), .clock(clock), .Dout(RegB_dout), .data(out_6));
  Button button_1 (.out(clock));
  ALU alu_1 (.OE(ALU_OE), .RegA(RegA_dout), .RegB(RegB_dout), .Dout(alu_1_dout), .data(out_11));  // open: Carry
  _8bitRegister OutputReg (
    .WE(RegA_WE_2), .OE(RegA_OE_2), .Din(alu_1_dout), .clock(clock), .Dout(OutputReg_dout), .data(out_10));
  Counter #(.Bits(2)) \u_程序计数器  (.en(PC_EN), .C(clock), .clr(1'b0), .out(PC[1:0]));  // open: ovf
  _8bitRegister IR (.WE(IR_WE), .OE(IR_OE), .Din(OutputReg_dout), .clock(clock), .Dout(IR_dout), .data(out_18));
  assign IR_dout[3:0] = PC_OE ? {2'b00, PC[1:0]} : 4'bz;  // Driver driver_1
  _8bitRegister MBR (
    .WE(MBR_WE), .OE(MBR_OE), .Din(OutputReg_dout), .clock(clock), .Dout(OutputReg_dout), .data(out_14));
  _4bitRegister MAR (.WE(MAR_WE), .OE(MAR_OE), .Din(IR_dout[3:0]), .clock(clock), .Dout(MAR_dout), .data(addr));
  EEPROMDualPort #(.AddrBits(4), .Bits(8)) eepromdualport_1 (
    .A(MAR_dout), .Din(OutputReg_dout), .str(Memory_WE), .C(clock), .ld(Memory_OE), .D(OutputReg_dout));

  assign PC[3:2] = 2'b00;

  // Notes on the sheet:
  //   内部数据总线
  //   内存缓存寄存器
  //   外部数据总线
  //   contents of eepromdualport_1 (hex, n*v repeats v):
  //   e,1f,20,3f,10*0,1,3
endmodule
