// Digital circuit 计算机体系结构自动化版.dig as structural Verilog
module \计算机体系结构自动化版  (
  input  clk,
  output [7:0] out_1,
  output [7:0] out_2,
  output [7:0] out_3,
  output [7:0] out_4,
  output [7:0] out_5,
  output [3:0] addr,
  output [3:0] PC,
  output [3:0] opcode,
  output [16:0] out_9,
  output [2:0] out_10
);

  wire [3:0] IR_data, MAR_dout;
  wire [7:0] alu_1_dout, IR_dout, OutputReg_dout, RegA_dout, RegB_dout;

  Counter #(.Bits(3)) counter_1 (.en(1'b1), .C(clk), .clr(1'b0), .out(out_10));  // open: ovf
  _8bitRegister RegA (
    .WE(out_9[10]), .OE(out_9[11]), .Din(OutputReg_dout), .clock(clk), .Dout(RegA_dout), .data(out_1));
  _8bitRegister RegB (
    .WE(out_9[12]), .OE(out_9[13]), .Din(OutputReg_dout), .clock(clk), .Dout(RegB_dout), .data(out_2));
  LookUpTable #(.Bits(17)) lookuptable_1 (
    .in0(out_10[0]), .in1(out_10[1]), .in2(out_10[2]), .in3(opcode[0]), .in4(opcode[1]), .out(out_9));
  ALU alu_1 (.OE(out_9[14]), .RegA(RegA_dout), .RegB(RegB_dout), .Dout(alu_1_dout), .data(out_4));  // open: Carry
  _8bitRegister OutputReg (
    .WE(out_9[15]), .OE(out_9[16]), .Din(alu_1_dout), .clock(clk), .Dout(OutputReg_dout), .data(out_3));
  Counter #(.Bits(2)) \u_程序计数器  (.en(out_9[1]), .C(clk), .clr(1'b0), .out(PC[1:0]));  // open: ovf
  _8bitRegister IR (
    .WE(out_9[2]), .OE(out_9[3]), .Din(OutputReg_dout), .clock(clk), .Dout(IR_dout), .data({opcode, IR_data}));
  assign IR_dout[3:0] = out_9[0] ? {2'b00, PC[1:0]} : 4'bz;  // Driver driver_1
  _8bitRegister MBR (
    .WE(out_9[6]), .OE(out_9[7]), .Din(OutputReg_dout), .clock(clk), .Dout(OutputReg_dout), .data(out_5));
  _4bitRegister MAR (.WE(out_9[4]), .OE(out_9[5]), .Din(IR_dout[3:0]), .clock(clk), .Dout(MAR_dout), .data(addr));
  EEPROMDualPort #(.AddrBits(4), .Bits(8)) eepromdualport_1 (
    .A(MAR_dout), .Din(OutputReg_dout), .str(out_9[8]), .C(clk), .ld(out_9[9]), .D(OutputReg_dout));

  assign PC[3:2] = 2'b00;

  // Other names for the same wires on the sheet: clock = clk; PC_OE = out_9[0]; PC_EN = out_9[1]; IR_WE = out_9[2];
  //   IR_OE = out_9[3]; MAR_WE = out_9[4]; MAR_OE = out_9[5]; MBR_WE = out_9[6]; MBR_OE = out_9[7];
  //   Memory_WE = out_9[8]; Memory_OE = out_9[9]; RegA_WE = out_9[10]; RegA_OE = out_9[11]; RegB_WE = out_9[12];
  //   RegB_OE = out_9[13]; ALU_OE = out_9[14]; Output_WE = out_9[15]; Output_OE = out_9[16]

  // Notes on the sheet:
  //   clk: Hz: 8
  //   contents of lookuptable_1 (hex, n*v repeats v):
  //   11,2,260,84,18,260,480,0,11,2,260,84,18,260,1080,0,11,2,260,84
  //   ,e800,0,0,0,11,2,260,84,18,10040,1a0
  //   时序控制
  //   内部数据总线
  //   内存缓存寄存器
  //   外部数据总线
  //   contents of eepromdualport_1 (hex, n*v repeats v):
  //   e,1f,20,3f,10*0,3,bb
  //   取指
  //   0x11   PC->MAR
  //   0x2     (PC)+1->PC
  //   0x260  Memory(MAR)->MBR
  //   0x84    MBR->IR
  //   LOAD_A
  //   0x18    addr(IR)->MAR
  //   0x260  Memory(MAR)->MBR
  //   0x480  MBR->RegA
  //   LOAD_B
  //   0x18    addr(IR)->MAR
  //   0x260  Memory(MAR)->MBR
  //   0x1080 MBR->RegB
  //   ADD
  //   0xE800     RegA,RegB->ALU->OutputReg
  //   STORE
  //   0x18     addr(IR)->MAR
  //   0x10040   OutputReg->MBR
  //   0x1A0   MBR->Memory(MAR)
  //   操作码    操作数地址
  //   0b 0000 1110   LOAD->A
  //   0b 0001 1111   LOAD->B
  //   0b 0010 0000	ADD
  //   0b 0011 1111   STORE
  //   0b 0000 0000  空操作
endmodule
