// Digital circuit 输入输出使能寄存器.dig as structural Verilog
module \输入输出使能寄存器  (
  input  clock,
  input  [7:0] Din,
  input  En,
  input  OE,
  output [7:0] Dout,
  output [7:0] data
);

  Register #(.Bits(8)) register_1 (.D(Din), .C(clock), .en(En), .Q(data));
  assign Dout = OE ? data : 8'bz;  // Driver driver_1

  // Notes on the sheet:
  //   OE: out enable
  //   data: 方便实验观察
endmodule
